// Logisim project Project2.circ as structural Verilog
module main (
);

  wire and_1_out, and_2_out, B0, B1, B2, B3, B4, B5, B6, B7, B8, B9, BL, BU, C0, C1, C2, CLK, not_1_out,
       or_8_out, panel_1_v, R0, R1, R3, R4, undriven, undriven_2, Valid;
  wire [2:0] counter_1_q;
  wire [3:0] inputbuffer_1_c0, panel_1_b3, register_2_q, register_3_q, register_4_q, register_5_q;

  Button n1 (.out(B1));
  Button n4 (.out(B4));
  Button n7 (.out(B7));
  Button L (.out(BL));
  Button n3 (.out(B3));
  Button n2 (.out(B2));
  Button n6 (.out(B6));
  Button n5 (.out(B5));
  Button n9 (.out(B9));
  Button n8 (.out(B8));
  Button U (.out(BU));
  Button n0 (.out(B0));
  or or_1 (R0, B3, B2, B1);
  or or_2 (R1, B6, B5, B4);
  or or_3 (R3, B9, B8, B7);
  or or_4 (R4, BU, B0, BL);
  or or_5 (C0, B1, B4, B7, BL);
  or or_6 (C1, B2, B5, B8, B0);
  or or_7 (C2, B3, B6, B9, BU);
  Clock clock_1 (.out(CLK));
  nand nand_1 (Valid, inputbuffer_1_c0[0], inputbuffer_1_c0[1], inputbuffer_1_c0[2], inputbuffer_1_c0[3]);
  // Probe on panel_1_b3
  Panel panel_1 (
    .R0(R0), .R1(R1), .R2(R3), .R3(R4), .C0(C0), .C1(C1), .C2(C2), .B3(panel_1_b3[0]), .B2(panel_1_b3[1]),
    .B1(panel_1_b3[2]), .B0(panel_1_b3[3]), .V(panel_1_v));
  LED Press (.in(panel_1_v));
  // Probe on inputbuffer_1_c0
  InputBuffer inputbuffer_1 (
    .B0(panel_1_b3[0]), .B1(panel_1_b3[1]), .B2(panel_1_b3[2]), .B3(panel_1_b3[3]), .V(panel_1_v),
    .in_6(not_1_out), .C0(inputbuffer_1_c0[0]), .C1(inputbuffer_1_c0[1]), .C2(inputbuffer_1_c0[2]),
    .C3(inputbuffer_1_c0[3]));
  not not_1 (not_1_out, CLK);
  Register #(.width(4)) register_1 (.D(register_2_q), .en(Valid), .clk(CLK));  // open: Q, clr
  Lock L1 ();
  Counter #(.max('h7), .width(3)) counter_1 (
    .count(or_8_out), .Q(counter_1_q), .up(undriven_2), .clk(CLK));  // open: load, D, carry, clr
  or or_8 (or_8_out, undriven, undriven_2);
  Register #(.width(4)) register_2 (.D(register_3_q), .en(Valid), .clk(CLK), .Q(register_2_q));  // open: clr
  LED Unlocked (.in(and_1_out));
  and and_1 (and_1_out, ~counter_1_q[0], ~counter_1_q[1], ~counter_1_q[2]);  // AND_Gate
  Register #(.width(4)) register_3 (.D(register_4_q), .en(Valid), .clk(CLK), .Q(register_3_q));  // open: clr
  LED Locked (.in(and_2_out));
  and and_2 (and_2_out, ~counter_1_q[0], ~counter_1_q[1], counter_1_q[2]);  // AND_Gate
  Register #(.width(4)) register_4 (.D(register_5_q), .en(Valid), .clk(CLK), .Q(register_4_q));  // open: clr
  Register #(.width(4)) register_5 (.D(inputbuffer_1_c0), .en(Valid), .clk(CLK), .Q(register_5_q));  // open: clr
endmodule

module Panel (
  input  R0,
  input  R1,
  input  R2,
  input  R3,
  input  C0,
  input  C1,
  input  C2,
  output B3,
  output B2,
  output B1,
  output B0,
  output V
);

  wire Eight, Five, Four, L, Nine, One, priority_encoder_1_gs, Seven, Six, Three, Two, U, xor_1_out,
       xor_2_out, Zero;
  wire [3:0] multiplexer_1_out, priority_encoder_1_out;

  and and_1 (One, R0, C0);
  and and_2 (Two, R0, C1);
  and and_3 (Three, R0, C2);
  and and_4 (L, R3, C0);
  and and_5 (U, R3, C2);
  and and_6 (Four, R1, C0);
  and and_7 (Five, R1, C1);
  and and_8 (Six, R1, C2);
  and and_9 (Zero, R3, C1);
  Priority_Encoder #(.select(4)) priority_encoder_1 (
    .in0(Zero), .in1(One), .in2(Two), .in3(Three), .in4(Four), .in5(Five), .in6(Six), .in7(Seven),
    .in8(Eight), .in9(Nine), .in10(L), .in11(U), .out(priority_encoder_1_out), .gs(priority_encoder_1_gs));  // open: in12, in13, in14, in15, en_out, en_in
  and and_10 (Seven, R2, C0);
  and and_11 (Eight, R2, C1);
  and and_12 (Nine, R2, C2);
  Multiplexer #(.width(4)) multiplexer_1 (
    .in1(priority_encoder_1_out), .out(multiplexer_1_out), .sel(priority_encoder_1_gs));  // open: in0
  ExactlyOne xor_1 (.out(xor_1_out), .in0(R0), .in1(R1), .in2(R2), .in3(R3));
  ExactlyOne xor_2 (.out(xor_2_out), .in0(C0), .in1(C1), .in2(C2));
  ExactlyOne xor_3 (.out(B3), .in0(Eight), .in1(Nine), .in2(L), .in3(Zero), .in4(U));
  ExactlyOne xor_4 (.out(B2), .in0(Four), .in1(Five), .in2(Six), .in3(Seven));
  ExactlyOne xor_5 (.out(B1), .in0(L), .in1(U), .in2(Two), .in3(Six), .in4(Three), .in5(Seven));
  ExactlyOne xor_6 (.out(B0), .in0(Three), .in1(Seven), .in2(Five), .in3(Nine), .in4(U), .in5(One));
  and and_13 (V, xor_1_out, xor_2_out);
endmodule

module InputBuffer (
  input  B0,
  input  B1,
  input  B2,
  input  B3,
  input  V,
  input  in_6,
  output C0,
  output C1,
  output C2,
  output C3
);

  wire and_1_out, d_ff_1_qn;
  wire [3:0] multiplexer_1_out;

  D_Flip_Flop d_ff_1 (.D(V), .clk(in_6), .Qn(d_ff_1_qn));  // open: Q, preset, reset
  Multiplexer #(.width(4)) multiplexer_1 (
    .in0(4'b1111), .in1({B3, B2, B1, B0}), .out(multiplexer_1_out), .sel(and_1_out));
  and and_1 (and_1_out, d_ff_1_qn, V);
  Register #(.width(4)) register_1 (.D(multiplexer_1_out), .en(1'b1), .clk(in_6), .Q({C3, C2, C1, C0}));  // open: clr

  // Other names for the same wires on the sheet: CLK = in_6
endmodule
